# Fritzing sketch MiniMonsterTruck (saved by Fritzing 0.9.2b)
breadboards: 1

parts:
  Arduino = Arduino Nano (Rev3.0)
  Motor_Driver_IC = L293D [package=THT]
  12V_DC = Power plug
  M1 = DC Motor
  R1_2W = Resistor [tolerance=±5% resistance=12 package=THT]
  M2 = DC Motor
  R2_2W = Resistor [tolerance=±5% resistance=12 package=THT]
  Bluetooth_Module = Bluetooth HC-05 Macho
  LED1 = smd LED [color="Red (633nm)" package="0805 [SMD]"]
  R3_1/4W = Resistor [tolerance=±5% resistance=150 package=THT]
  Ultrasonic_Sensor = SRF05 Ultrasonic Rangefinder

nets:
  GND: Arduino.GND, Motor_Driver_IC.0V, 12V_DC.GND, Bluetooth_Module.GND, R3_1/4W.Pin_1, Ultrasonic_Sensor.GND
  N1: Arduino.D2, Ultrasonic_Sensor.Echo
  N2: Arduino.D3, Motor_Driver_IC.Enable_2
  N3: Arduino.D4, Ultrasonic_Sensor.Trig
  N4: Arduino.D5, Motor_Driver_IC.In_3
  N5: Arduino.D6, Motor_Driver_IC.In_4
  N6: Arduino.D7, Bluetooth_Module.RXD
  N7: Arduino.D8, Bluetooth_Module.TXD
  N8: Arduino.D9, Motor_Driver_IC.In_2
  N9: Arduino.D10, Motor_Driver_IC.In_1
  N10: Arduino.D11/MOSI, Motor_Driver_IC.Enable_1
  N11: Arduino.D12/MISO, LED1.anode
  VIN: Arduino.VIN, Motor_Driver_IC.+Vmotor, 12V_DC.VCC
  VCC: Arduino.5V, Motor_Driver_IC.+V, Bluetooth_Module.VCC, Ultrasonic_Sensor.VCC
  N12: Motor_Driver_IC.Out_1_(_Controlled_by_Enable_1_), M1.pin_2
  N13: Motor_Driver_IC.Out_3_(_Controlled_by_Enable_2_), M2.pin_2
  N14: M1.pin_1, R1_2W.Pin_1
  N15: M2.pin_1, R2_2W.Pin_0
